# Fritzing sketch Vehicle Tracking System (saved by Fritzing 0.9.3b)
breadboards: 1

parts:
  Mod1 = Amica NodeMCU DevKit 1.0
  M1 = NEO-6M GPS Module [part_number=GY-GPS6MV2]
  GSM_SIM_GPSR_SMS_SIM900_SIM1 = SIM800L [package=THT]
  LED1 = smd LED [color="Red (633nm)" package="1206 [SMD]"]  # not connected
  R1 = Resistor [tolerance=±5% resistance=1k package="2010 [SMD]"]
  S1 = Pushbutton [package="[SMD]"]
  R2 = Resistor [tolerance=±5% resistance=1k package="0603 [SMD]"]
  LED2 = smd LED [color="Blue (525nm)" package="0805 [SMD]"]
  R3 = Resistor [tolerance=±5% resistance=1k package="0603 [SMD]"]
  BAT1 = 18650 battery holder [package=battery-18650-kit]
  M2 = RioRand LM2596

nets:
  N1: Mod1.pin1, Mod1.pin_10, Mod1.pin_26, S1.Pin_3, S1.Pin_4
  N2: Mod1.pin2, Mod1.pin_9, Mod1.pin_25, Mod1.pin_29, M1.GND, GSM_SIM_GPSR_SMS_SIM900_SIM1.GND#5, R2.Pin_0, LED2.cathode, M2.Pin_4
  N3: Mod1.pin5, S1.Pin_1, S1.Pin_2, R2.Pin_1
  N4: Mod1.pin7, GSM_SIM_GPSR_SMS_SIM900_SIM1.SIM_RXD, R1.Pin_1
  N5: Mod1.pin8, GSM_SIM_GPSR_SMS_SIM900_SIM1.SIM_TXD
  N6: Mod1.pin_12, M1.Tx
  N7: Mod1.pin_13, M1.Rx
  N8: Mod1.pin_14, GSM_SIM_GPSR_SMS_SIM900_SIM1.RST
  N9: Mod1.pin_15, R3.Pin_0
  N10: Mod1.pin_30, M1.Vcc, M2.Pin_3
  N11: GSM_SIM_GPSR_SMS_SIM900_SIM1.5V, BAT1.+
  N12: GSM_SIM_GPSR_SMS_SIM900_SIM1.GND#1, BAT1.-
  N13: LED2.anode, R3.Pin_1

custom parts:
  Amica NodeMCU DevKit 1.0: Amica NodeMCU DevKit 1.0 Development Kit based on ESP8266 ESP-12E, integating GPIO, PWM, IIC, 1-Wire and ADC all in one board. Links: NodeMCU information page Github
  NEO-6M GPS Module: GY-GPS6MV2 NEO-6M GPS Module Module based on U-blox NEO-6M GPS engine, incorporating regulator for 3.3-5V DC input, MS621FE-compatible rechargeable battery for backup and EEPROM for storing configuration settings. Links: NEO-6 series product information page NEO-6 Datasheet
  18650 battery holder: 18650 Battery Holder
